# Fritzing sketch MotorDriver (saved by Fritzing 0.9.3b)
circuit board: 6.0726cm x 7.86062cm
breadboards: 1

parts:
  M2 = Screw terminal - 2 pins [package=THT]
  M1 = Screw terminal - 2 pins [package=THT]
  VCC = Screw terminal - 2 pins [package=THT]
  VBAT = Screw terminal - 2 pins [package=THT]
  Teensy3_2_Carrier = IC, DIP package, 28 pins [chip_label=IC]
  TB6612FNG_Carrier = IC, DIP package, 16 pins [chip_label=IC]

nets:
  N1: M2.pin1, TB6612FNG_Carrier.pin6
  N2: M2.pin2, TB6612FNG_Carrier.pin7
  N3: M1.pin1, TB6612FNG_Carrier.pin4
  N4: M1.pin2, TB6612FNG_Carrier.pin5
  N5: VCC.pin1, Teensy3_2_Carrier.pin28, TB6612FNG_Carrier.pin2, TB6612FNG_Carrier.pin13
  N6: VCC.pin2, VBAT.pin2, Teensy3_2_Carrier.pin1, TB6612FNG_Carrier.pin3, TB6612FNG_Carrier.pin9
  N7: VBAT.pin1, TB6612FNG_Carrier.pin1
  N8: Teensy3_2_Carrier.pin4, TB6612FNG_Carrier.pin14
  N9: Teensy3_2_Carrier.pin5, TB6612FNG_Carrier.pin15
  N10: Teensy3_2_Carrier.pin6, TB6612FNG_Carrier.pin12
  N11: Teensy3_2_Carrier.pin7, TB6612FNG_Carrier.pin11
  N12: Teensy3_2_Carrier.pin24, TB6612FNG_Carrier.pin16
  N13: Teensy3_2_Carrier.pin25, TB6612FNG_Carrier.pin10
