# Fritzing sketch Teensy-Motor-Controller (saved by Fritzing 0.9.3b)
circuit board: 6.82707cm x 6.64502cm

parts:
  Teensy = Teensy 3.1
  Motor-Driver = Motor Driver 1A Dual TB6612FNG
  C1 = Electrolytic Capacitor [capacitance=0.47mF voltage=10V package="100 mil [THT, electrolytic]"]
  VBAT = screw terminal, 2 pins
  VIN = screw terminal, 2 pins
  M1J = screw terminal, 2 pins
  M2C = screw terminal, 2 pins
  M2J = male pin header, 6 pins [form="♂ (male)"]
  M1J_2 = male pin header, 6 pins [form="♂ (male)"]
  C2 = Electrolytic Capacitor [capacitance=10µF voltage=10V package="100 mil [THT, electrolytic]"]
  C3 = Electrolytic Capacitor [capacitance=100nF package="100 mil [THT, electrolytic]"]
  Logic_Shifter = Logic Level Converter
  3V3_Regulator = V_REG_LD1117VXX [package=78xxl]

nets:
  GND: Teensy.GND, Motor-Driver.GND, C1.-, VBAT.pin2, VIN.pin2, M2J.pin6, M1J_2.pin6, C2.-, C3.-, Logic_Shifter.GND, 3V3_Regulator.GND
  N1: Teensy.D2, Logic_Shifter.TX_HV
  N2: Teensy.D3, Logic_Shifter.TX2_HV
  N3: Teensy.D4, Logic_Shifter.RX2_LV
  N4: Teensy.D5, Logic_Shifter.RX_LV
  N5: Teensy.A0/D14, Motor-Driver.AIN1
  N6: Teensy.A1/D15, Motor-Driver.AIN2
  N7: Teensy.A2/D16, Motor-Driver.BIN1
  N8: Teensy.A3/D17, Motor-Driver.BIN2
  N9: Teensy.A6/D20, Motor-Driver.PWMA
  N10: Teensy.A7/D21, Motor-Driver.PWMB
  3V3/5V: Teensy.Vin, Motor-Driver.VCC, Motor-Driver.STBY, VIN.pin1, M2J.pin5, M1J_2.pin5, C2.+, C3.+, Logic_Shifter.LV, Logic_Shifter.HV, 3V3_Regulator.OUT, 3V3_Regulator.IN
  M2_1: Motor-Driver.B01, M2C.pin1, M2J.pin1
  M2_2: Motor-Driver.B02, M2C.pin2, M2J.pin2
  M1_2: Motor-Driver.A02, M1J.pin2, M1J_2.pin2
  M1_1: Motor-Driver.A01, M1J.pin1, M1J_2.pin1
  VBAT: Motor-Driver.VM, C1.+, VBAT.pin1
  M2_EN1: M2J.pin3, Logic_Shifter.TX2_LV
  M2_EN2: M2J.pin4, Logic_Shifter.RX_HV
  M1_EN1: M1J_2.pin3, Logic_Shifter.TX_LV
  M1_EN2: M1J_2.pin4, Logic_Shifter.RX2_HV
